# Fritzing sketch atmega328-bb (saved by Fritzing 1.0.3b)
breadboards: 1

parts:
  U1 = atmega328 [package=dip]
  C2 = Electrolytic Capacitor [capacitance=100nF voltage=35V package="0405 [SMD, electrolytic]"]
  J1 = AVR ISP 6 Pin [package=2x3]  # not connected
  JP1 = Header 6 [package=1x06-smd]  # not connected
  IC1 = Voltage Regulator [package=78xxl]  # not connected

nets:
  N1: U1.VCC, C2.+
  N2: U1.GND#7, C2.-
